# Fritzing sketch double_stepper_motor_Arduino_v03 (saved by Fritzing 0.9.3b)
breadboards: 1

parts:
  C2 = Electrolytic Capacitor [capacitance=100µF package="200 mil [THT, electrolytic]"]
  M1 = Stepper Motor - Bipolar
  C1 = Electrolytic Capacitor [capacitance=100µF package="200 mil [THT, electrolytic]"]
  Part8 = GY-VL53L0XV2 Laser Ranger Module
  M2 = Stepper Motor - Bipolar
  Pololu_A2 = Pololu A4988 [package=SO16]
  JACK1 = 2.1mm Barrel Jack with Terminal Block
  Pololu_A1 = Pololu A4988 [package=SO16]
  Part6 = Arduino Mega 2560 (Rev3)

nets:
  N1: C2.-, C1.-, Pololu_A2.GND#14, JACK1.NEG, Pololu_A1.GND#14
  N2: C2.+, C1.+, Pololu_A2.VMOT, JACK1.POS, Pololu_A1.VMOT
  N3: M1.A, Pololu_A1.2B
  N4: M1.C, Pololu_A1.2A
  N5: M1.B, Pololu_A1.1A
  N6: M1.D, Pololu_A1.1B
  VDD: Part8.VCC, Pololu_A2.VDD, Pololu_A1.VDD, Part6.5V
  GND: Part8.GND, Pololu_A2.GND#8, Pololu_A1.GND#8, Part6.GND
  N7: Part8.SCL, Part6.D21/SCL
  N8: Part8.SDA, Part6.D20/SDA
  N9: M2.A, Pololu_A2.2B
  N10: M2.C, Pololu_A2.2A
  N11: M2.B, Pololu_A2.1A
  N12: M2.D, Pololu_A2.1B
  N13: Pololu_A2.MS1, Part6.D2_PWM
  N14: Pololu_A2.MS2, Part6.D3_PWM
  N15: Pololu_A2.RESET, Pololu_A2.SLEEP
  N16: Pololu_A2.STEP, Part6.D4_PWM
  N17: Pololu_A2.DIR, Part6.D47
  N18: Pololu_A1.MS1, Part6.D6_PWM
  N19: Pololu_A1.MS2, Part6.D7_PWM
  N20: Pololu_A1.RESET, Pololu_A1.SLEEP
  N21: Pololu_A1.STEP, Part6.D5_PWM
  N22: Pololu_A1.DIR, Part6.D37

custom parts:
  GY-VL53L0XV2 Laser Ranger Module: The GY-VL53L0XV2 is based on the VL53L0X from ST Microelectronics, a time-of-flight ranging system integrated into a compact module.
